// Logisim project Lab3.circ as structural Verilog
module HalfAdder (
  input  x,
  input  y,
  output S,
  output C
);

  wire and_1_out, and_2_out, not_1_out, not_2_out;

  not not_1 (not_1_out, x);
  not not_2 (not_2_out, y);
  and and_1 (and_1_out, not_1_out, y);
  and and_2 (and_2_out, x, not_2_out);
  and and_3 (C, x, y);
  or or_1 (S, and_1_out, and_2_out);

  // Notes on the sheet:
  //   Half Adder
endmodule

module FullAdder (
  input  x,
  input  y,
  input  Cin,
  output Zo,
  output Cout
);

  wire and_1_out, and_2_out, and_3_out, and_4_out, and_5_out, and_6_out, and_7_out, not_1_out, not_2_out,
       not_3_out;

  not not_1 (not_1_out, x);
  not not_2 (not_2_out, y);
  not not_3 (not_3_out, Cin);
  and and_1 (and_1_out, not_1_out, not_2_out, Cin);
  and and_2 (and_2_out, not_1_out, y, not_3_out);
  and and_3 (and_3_out, x, not_2_out, not_3_out);
  and and_4 (and_4_out, x, y, Cin);
  and and_5 (and_5_out, y, Cin);
  and and_6 (and_6_out, x, Cin);
  and and_7 (and_7_out, x, y);
  or or_1 (Zo, and_1_out, and_2_out, and_3_out, and_4_out);
  or or_2 (Cout, and_5_out, and_6_out, and_7_out);
endmodule

module TestCircuit (
  input  in_1,
  input  in_2,
  input  in_3,
  input  [3:0] in_4,
  input  [3:0] in_5,
  input  in_6,
  input  [3:0] x,
  input  [3:0] y,
  output out_9,
  output out_10,
  output [3:0] sum,
  output out_12,
  output out_13,
  output out_14,
  output [3:0] z,
  output cout
);

  wire xor_1_out;

  HalfAdder halfadder_1 (.x(in_2), .y(in_3), .S(out_9), .C(out_10));
  FullAdder fulladder_1 (.x(in_2), .y(in_3), .Cin(in_6), .Zo(out_13), .Cout(out_14));
  RippleCarry ripplecarry_1 (.in_1(x), .in_2(y), .z(z), .Cout(cout));  // open: Cin
  xor xor_1 (xor_1_out, in_1, in_5[0]);
  xor xor_2 (xor_1_out, in_1, in_5[1]);
  xor xor_3 (xor_1_out, in_1, in_5[2]);
  xor xor_4 (xor_1_out, in_1, in_5[3]);
  // ALU alu_1: pin names not known; wires that end beside it: in_4, xor_1_out, in_1, sum, out_12

  // Other names for the same wires on the sheet: a0 = in_5[0]; a1 = in_5[1]; a2 = in_5[2]; a3 = in_5[3]

  // Notes on the sheet:
  //   Test Circuit
endmodule

module RippleCarry (
  input  [3:0] in_1,
  input  [3:0] in_2,
  input  Cin,
  output [3:0] z,
  output Cout
);

  wire c0, c01, c02;

  FullAdder fulladder_1 (.x(in_1[0]), .y(in_2[0]), .Cin(Cin), .Zo(z[0]), .Cout(c0));
  FullAdder fulladder_2 (.x(in_1[1]), .y(in_2[1]), .Cin(c0), .Zo(z[1]), .Cout(c01));
  FullAdder fulladder_3 (.x(in_1[2]), .y(in_2[1]), .Cin(c01), .Zo(z[2]), .Cout(c02));
  FullAdder fulladder_4 (.x(in_1[3]), .y(in_2[1]), .Cin(c02), .Zo(z[3]), .Cout(Cout));

  // Other names for the same wires on the sheet: x0 = in_1[0]; x1 = in_1[1]; x2 = in_1[2]; x3 = in_1[3]; y0 = in_2[0];
  //   y1 = in_2[1]; y2 = in_2[2]; y3 = in_2[3]

  // Notes on the sheet:
  //   Ripple Carry - 4 Bit
endmodule

module ALU (
  input  in_1,
  input  [3:0] in_2,
  input  [3:0] in_3,
  output [3:0] z,
  output c4
);

  wire c0, c01, c02, xor_1_out, xor_2_out, xor_3_out, xor_4_out;

  xor xor_1 (xor_1_out, in_1, in_2[0]);
  xor xor_2 (xor_2_out, in_1, in_2[1]);
  xor xor_3 (xor_3_out, in_1, in_2[2]);
  xor xor_4 (xor_4_out, in_1, in_2[3]);
  FullAdder fulladder_1 (.x(xor_1_out), .y(in_3[0]), .Cin(in_1), .Zo(z[0]), .Cout(c0));
  FullAdder fulladder_2 (.x(xor_2_out), .y(in_3[1]), .Cin(c0), .Zo(z[1]), .Cout(c01));
  FullAdder fulladder_3 (.x(xor_3_out), .y(in_3[1]), .Cin(c01), .Zo(z[2]), .Cout(c02));
  FullAdder fulladder_4 (.x(xor_4_out), .y(in_3[1]), .Cin(c02), .Zo(z[3]), .Cout(c4));

  // Other names for the same wires on the sheet: x0 = in_2[0]; x1 = in_2[1]; x2 = in_2[2]; x3 = in_2[3]; y0 = in_3[0];
  //   y1 = in_3[1]; y2 = in_3[2]; y3 = in_3[3]

  // Notes on the sheet:
  //   Arithmetic Logic Unit
endmodule
