// Logisim project MultuplexerLab.circ as structural Verilog: 3 circuits, main circuit main
module main (
  input  Cin,
  input  A,
  input  B,
  input  s,
  output Cout,
  output sum0,
  output Cout0,
  output sum1,
  output Sum,
  output Cout1,
  output mode
);

  wire Cout0_t, Cout1_t, sum0_t, sum1_t;

  muxfulladder muxfulladder_1 (.Cin(Cin), .A(A), .B(B), .out_4(sum0), .out_5(Cout0));
  muxdecoder muxdecoder_1 (.Cin(Cin), .A(A), .B(B), .out_4(sum1), .out_5(Cout1));
  Multiplexer multiplexer_1 (.in0(sum0_t), .in1(sum1_t), .out(Sum), .sel(s));
  Multiplexer multiplexer_2 (.in0(Cout0_t), .in1(Cout1_t), .out(Cout), .sel(s));

  assign mode = s;
endmodule

module muxfulladder (
  input  Cin,
  input  A,
  input  B,
  output out_4,
  output out_5
);

  Multiplexer #(.select(3)) multiplexer_1 (
    .in0(1'b0), .in1(1'b0), .in2(1'b0), .in3(1'b0), .in4(1'b1), .in5(1'b1), .in6(1'b1), .in7(1'b1),
    .out(out_4), .sel({B, A, Cin}));
  Multiplexer #(.select(3)) multiplexer_2 (
    .in0(1'b1), .in1(1'b1), .in2(1'b1), .in3(1'b1), .in4(1'b1), .in5(1'b1), .in6(1'b1), .in7(1'b1),
    .out(out_5), .sel({B, A, Cin}));

  // Other names for the same wires on the sheet: Cout = out_4; sum = out_5

  // Notes on the sheet:
  //   only thing i didnt do is truth table values for full adder, can do at home)
endmodule

module muxdecoder (
  input  Cin,
  input  A,
  input  B,
  output out_4,
  output out_5
);

  wire decoder_1_out3, decoder_1_out5, decoder_1_out6, decoder_1_out7, decoder_2_out1, decoder_2_out2,
       decoder_2_out4, decoder_2_out7;

  Decoder #(.select(3)) decoder_1 (
    .out3(decoder_1_out3), .out5(decoder_1_out5), .out6(decoder_1_out6), .out7(decoder_1_out7),
    .sel({B, A, Cin}));  // open: out0, out1, out2, out4, en
  or or_1 (out_4, decoder_1_out3, decoder_1_out5, decoder_1_out6, decoder_1_out7);
  Decoder #(.select(3)) decoder_2 (
    .out1(decoder_2_out1), .out2(decoder_2_out2), .out4(decoder_2_out4), .out7(decoder_2_out7),
    .sel({B, A, Cin}));  // open: out0, out3, out5, out6, en
  or or_2 (out_5, decoder_2_out1, decoder_2_out2, decoder_2_out4, decoder_2_out7);

  // Other names for the same wires on the sheet: Cout = out_4; sum = out_5

  // Notes on the sheet:
  //   m(3,5,6,7)
  //   m(1,2,4,7)
endmodule
