// Logisim project final.circ as structural Verilog: 1 circuit, main circuit mainfinal
module mainfinal (
  input  Input_1,
  input  reset
);

  wire b0, b1, b2, b3, b4, b5, b6, c0, c1, c2, c3, c4, c5, c6, clck, G, pedestrian_button_1_en, R, undriven,
       v0, v1, v2, v3, Y;
  wire [1:0] fsm_1_nxtstate, register_1_q;
  wire [3:0] DownCounter_Template_1_count;
  wire [7:0] HEX0, HEX1;
  wire [7:7] Bin2Hex_1_hex0, Bin2Hex_1_hex1;

  maintrafficlight maintrafficlight_1 (.en(undriven));
  pedestrian_button pedestrian_button_1 (.en(pedestrian_button_1_en));  // open: counter
  // RGBLED RGBLED_1: pin names not known; wires that end beside it: R
  // RGBLED RGBLED_2: pin names not known; wires that end beside it: Y, Y
  // RGBLED RGBLED_3: pin names not known; wires that end beside it: G
  FSM fsm_1 (
    .en(undriven), .count_zero(pedestrian_button_1_en), .state(register_1_q), .G(G), .Y(Y), .R(R),
    .nxtstate(fsm_1_nxtstate));  // open: rst
  Register #(.width(2)) register_1 (.D(fsm_1_nxtstate), .en(1'b1), .clk(clck), .Q(register_1_q));  // open: clr
  _7_Segment_Display #(.active("false")) L_7_Segment_Display_1 (
    .g(HEX1[6]), .f(HEX1[5]), .a(HEX1[0]), .b(HEX1[1]), .e(HEX1[4]), .d(HEX1[3]), .c(HEX1[2]), .dp(HEX1[7]));
  _7_Segment_Display #(.active("false")) L_7_Segment_Display_2 (
    .g(HEX0[6]), .f(HEX0[5]), .a(HEX0[0]), .b(HEX0[1]), .e(HEX0[4]), .d(HEX0[3]), .c(HEX0[2]), .dp(HEX0[7]));
  DownCounter_v1 downcounter_v1_1 (.en(R), .clk(clck), .count({v3, v2, v1, v0}));
  Bin2Hex bin2hex_1 (.v3(v3), .v2(v2), .v1(v1), .v0(v0), .HEX1(HEX1), .HEX0(HEX0));
  Clock clock_1 (.out(clck));
  _7_Segment_Display #(.active("false")) L_7_Segment_Display_3 (
    .g(b6), .f(b5), .a(b0), .b(b1), .e(b4), .d(b3), .c(b2), .dp(1'b1));
  DownCounter_Template1 DownCounter_Template_1 (
    .enable(Input_1), .clock(clck), .reset(reset), .count(DownCounter_Template_1_count));
  _7_Segment_Display #(.active("false")) L_7_Segment_Display_4 (
    .g(c6), .f(c5), .a(c0), .b(c1), .e(c4), .d(c3), .c(c2), .dp(1'b1));
  Bin2Hex1 Bin2Hex_1_dup2 (
    .v3(DownCounter_Template_1_count[3]), .v2(DownCounter_Template_1_count[2]),
    .v1(DownCounter_Template_1_count[1]), .v0(DownCounter_Template_1_count[0]),
    .HEX1({Bin2Hex_1_hex1[7], b6, b5, b4, b3, b2, b1, b0}),
    .HEX0({Bin2Hex_1_hex0[7], c6, c5, c4, c3, c2, c1, c0}));

  // Notes on the sheet:
  //   Traffic Light A
  //   Counter Display
  //   Counter Display
endmodule
