// Logisim project Lab8.circ as structural Verilog: 3 circuits, main circuit main
module main (
  input  [1:0] Input_bus_1,
  output Output_1,
  output Output_2,
  output Output_3
);

  wire clock_1_out;
  wire [2:0] counter_1_q;

  Clock clock_1 (.out(clock_1_out));
  Counter #(.max('h7), .width(3)) counter_1 (
    .Q(counter_1_q), .clk(clock_1_out));  // open: load, D, count, carry, up, clr
  Multiplexer #(.select(2), .width(3)) multiplexer_1 (
    .in0(counter_1_q), .in1({2'b00, counter_1_q[0]}), .in2({1'b0, counter_1_q[1], 1'b0}),
    .out({Output_3, Output_2, Output_1}), .sel(Input_bus_1));  // open: in3
endmodule

module redblink (
  input  in_1,
  output out_2
);

  wire clock_1_out;

  Clock #(.phaseOffset(5)) clock_1 (.out(clock_1_out));
  Counter #(.max('h1), .width(1)) counter_1 (
    .D(in_1), .Q(out_2), .clk(clock_1_out));  // open: load, count, carry, up, clr
endmodule

module cycle (
  output Output_1,
  output Output_2,
  output Output_3
);

  wire clock_1_out;

  Clock clock_1 (.out(clock_1_out));
  Counter #(.max('h7), .width(3)) counter_1 (
    .Q({Output_3, Output_2, Output_1}), .clk(clock_1_out));  // open: load, D, count, carry, up, clr
endmodule
